# Fritzing sketch main_board (saved by Fritzing 0.9.3b)
circuit board: 8.46667cm x 5.64444cm
breadboards: 1

parts:
  Pololu_A1 = Pololu A4988 [package=SO16]
  M1 = fc-51 [package=THT]
  C1 = Capacitor Polarized [package=cpol-radial-100uf-25v]
  M2 = Stepper Motor - Bipolar
  Componente2 = Arduino Nano (Rev3.0)
  S1 = Pushbutton [package="[THT]"]
  J1 = Basic Servo
  J2 = Basic Servo

nets:
  N1: Pololu_A1.RESET, Pololu_A1.SLEEP
  N2: Pololu_A1.STEP, Componente2.D4
  N3: Pololu_A1.DIR, Componente2.D5
  GND: Pololu_A1.GND#8, M1.pin2, J1.gnd, J2.gnd
  VCC: Pololu_A1.VDD, M1.pin3, Componente2.D8, S1.Pin_1, S1.Pin_2, S1.Pin_3, S1.Pin_4, J1.vcc, J2.vcc
  N4: Pololu_A1.1B, M2.D
  N5: Pololu_A1.1A, M2.B
  N6: Pololu_A1.2A, M2.C
  N7: Pololu_A1.2B, M2.A
  N8: Pololu_A1.GND#14, C1.-
  N9: Pololu_A1.VMOT, C1.+
  N10: M1.pin1, Componente2.D6
  N11: Componente2.D9, J1.pulse
  N12: Componente2.D10, J2.pulse
