# Fritzing sketch main_board_pro_mini (saved by Fritzing 0.9.3b)
circuit board: 8.46667cm x 5.64444cm
breadboards: 2

parts:
  Pololu_A1 = Pololu A4988 [package=SO16]
  Sensor_de_bola = fc-51 [package=THT]  # not connected
  C1 = Capacitor Polarized [package=cpol-radial-100uf-25v]
  M2 = Stepper Motor - Bipolar
  Elevação = Basic Servo  # not connected
  920KV_Motor2 = DJI 920 KV Motor
  M3 = ESC
  M4 = ESC
  920KV_Motor3 = DJI 920 KV Motor
  Azimute = Basic Servo  # not connected
  PAUSE_BUTTON = Round Pushbutton  # not connected
  Grove1 = Grove 4 Digit Display  # not connected
  Componente4 = Arduino Nano (Rev3.0)  # not connected

nets:
  N1: Pololu_A1.RESET, Pololu_A1.SLEEP
  N2: Pololu_A1.1B, M2.D
  N3: Pololu_A1.1A, M2.B
  N4: Pololu_A1.2A, M2.C
  N5: Pololu_A1.2B, M2.A
  N6: Pololu_A1.GND#14, Pololu_A1.VMOT, C1.+, C1.-
  N7: 920KV_Motor2.w, M3.W
  N8: 920KV_Motor2.v, M3.V
  N9: 920KV_Motor2.u, M3.U
  GND: M3.GND, M4.GND
  N10: M4.U, 920KV_Motor3.u
  N11: M4.V, 920KV_Motor3.v
  N12: M4.W, 920KV_Motor3.w

custom parts:
  DJI 920 KV Motor: DJI Brushless Outrunner 2212/920K Motor F330-550
